// Logisim project Proj 1.circ as structural Verilog: 8 circuits, main circuit main
module main (
  input  [31:0] FromMem,
  output WED
);

  wire clock_1_out, decoder_1_dummywbmux, decoder_1_dummywed, decoder_1_immmux,
       decoder_1_write_enable_register, isolate34_1_wbmux_out, isolate34_1_wer_out, isolator_2_3_1_ie_out,
       isolator_2_3_1_wbmux_out, isolator_2_3_1_wed_out, isolator_2_3_1_wer_out, registerfile_1_p3;
  wire [3:0] decoder_1_dummyalu, isolator_2_3_1_op_out;
  wire [4:0] decoder_1_rd, decoder_1_rs, decoder_1_rt, decoder_1_shamt, isolate34_1_rd_out,
       isolator_2_3_1_rd_out, isolator_2_3_1_rs_out, isolator_2_3_1_rt_out, isolator_2_3_1_sa_out,
       registerfile_1_p4;
  wire [15:0] decoder_1_imm, isolator_2_3_1_imm_out;
  wire [31:0] bit_extender_1_out, count_1_1_pc_4, forward_1_forwarded, forward_2_forwarded,
       isolate12_1_instr_out, isolate12_1_pc_out, isolate34_1_c_out, isolate34_1_pc_out,
       isolator_2_3_1_a_out, isolator_2_3_1_b_out, isolator_2_3_1_pc_out, mips_alu_1_p5, mipsprogramrom_1_p2,
       multiplexer_1_out, multiplexer_2_out, register_1_q, registerfile_1_p1, registerfile_1_p7,
       registerfile_1_p8;

  Clock clock_1 (.out(clock_1_out));
  Count__1 count_1_1 (.PC(register_1_q), .PC_4(count_1_1_pc_4));
  Register #(.width(32)) register_1 (.D(count_1_1_pc_4), .Q(register_1_q), .clk(clock_1_out));  // open: en, clr
  // MIPSProgramROM mipsprogramrom_1: pin names not known; wires that end beside it: register_1_q, mipsprogramrom_1_p2
  Isolate12 isolate12_1 (
    .PC_in(register_1_q), .Instr_in(mipsprogramrom_1_p2), .clock(clock_1_out), .PC_out(isolate12_1_pc_out),
    .Instr_out(isolate12_1_instr_out));
  Decoder decoder_1 (
    .Instr(isolate12_1_instr_out), .Imm(decoder_1_imm), .rs(decoder_1_rs), .rt(decoder_1_rt),
    .rd(decoder_1_rd), .DummyALU(decoder_1_dummyalu), .shamt(decoder_1_shamt), .ImmMux(decoder_1_immmux),
    .DummyWBMUX(decoder_1_dummywbmux), .Write_Enable_Register(decoder_1_write_enable_register),
    .DummyWED(decoder_1_dummywed));
  // RegisterFile registerfile_1: pin names not known; wires that end beside it: registerfile_1_p1, clock_1_out, registerfile_1_p3, registerfile_1_p4, decoder_1_rs, decoder_1_rt, registerfile_1_p7, registerfile_1_p8
  Isolator_2_3 isolator_2_3_1 (
    .rs_in(decoder_1_rs), .rt_in(decoder_1_rs), .PC_in(isolate12_1_pc_out), .Imm_in(decoder_1_imm),
    .A_in(registerfile_1_p7), .B_in(registerfile_1_p8), .rd_in(decoder_1_rd), .op_in(decoder_1_dummyalu),
    .sa_in(decoder_1_shamt), .IE_in(decoder_1_immmux), .WBMUX_in(decoder_1_dummywbmux),
    .WER_in(decoder_1_write_enable_register), .WED_in(decoder_1_dummywed), .clock(clock_1_out),
    .rs_out(isolator_2_3_1_rs_out), .rt_out(isolator_2_3_1_rt_out), .PC_out(isolator_2_3_1_pc_out),
    .Imm_out(isolator_2_3_1_imm_out), .A_out(isolator_2_3_1_a_out), .B_out(isolator_2_3_1_b_out),
    .rd_out(isolator_2_3_1_rd_out), .op_out(isolator_2_3_1_op_out), .sa_out(isolator_2_3_1_sa_out),
    .IE_out(isolator_2_3_1_ie_out), .WBMUX_out(isolator_2_3_1_wbmux_out), .WER_out(isolator_2_3_1_wer_out),
    .WED_out(isolator_2_3_1_wed_out));
  Forward forward_1 (
    .Out2(registerfile_1_p1), .rd2(registerfile_1_p4), .rd1(isolate34_1_rd_out), .Out1(isolate34_1_c_out),
    .rs(isolator_2_3_1_rs_out), .Out0(isolator_2_3_1_a_out), .Forwarded(forward_1_forwarded));
  Forward forward_2 (
    .Out2(registerfile_1_p1), .rd2(registerfile_1_p4), .rd1(isolate34_1_rd_out), .Out1(isolate34_1_c_out),
    .rs(isolator_2_3_1_rt_out), .Out0(isolator_2_3_1_b_out), .Forwarded(forward_2_forwarded));
  assign bit_extender_1_out = {{16{1'b0}}, isolator_2_3_1_imm_out};  // Bit_Extender bit_extender_1
  Multiplexer #(.width(32), .enable("false")) multiplexer_1 (
    .in0(forward_2_forwarded), .in1(bit_extender_1_out), .out(multiplexer_1_out), .sel(isolator_2_3_1_ie_out));
  // Mips_ALU mips_alu_1: pin names not known; wires that end beside it: forward_1_forwarded, multiplexer_1_out, isolator_2_3_1_op_out, isolator_2_3_1_sa_out, mips_alu_1_p5
  Isolate_45 isolate_45_1 (
    .C_in(multiplexer_2_out), .PC_in(isolate34_1_pc_out), .rd_in(isolate34_1_rd_out),
    .WER_in(isolate34_1_wer_out), .clock(clock_1_out), .C_out(registerfile_1_p1), .rd_out(registerfile_1_p4),
    .WER_out(registerfile_1_p3));  // open: PC_out
  Isolate34 isolate34_1 (
    .C_in(mips_alu_1_p5), .PC_in(isolator_2_3_1_pc_out), .rd_in(isolator_2_3_1_rd_out),
    .WBMUX_in(isolator_2_3_1_wbmux_out), .WER_in(isolator_2_3_1_wer_out), .WED_in(isolator_2_3_1_wed_out),
    .clock(clock_1_out), .C_out(isolate34_1_c_out), .PC_out(isolate34_1_pc_out), .rd_out(isolate34_1_rd_out),
    .WBMUX_out(isolate34_1_wbmux_out), .WER_out(isolate34_1_wer_out), .WED_out(WED));
  Multiplexer #(.width(32), .enable("false")) multiplexer_2 (
    .in0(isolate34_1_c_out), .in1(FromMem), .out(multiplexer_2_out), .sel(isolate34_1_wbmux_out));
endmodule

module Count__1 (
  input  [31:0] PC,
  output [31:0] PC_4
);

  // Incrementer incrementer_1: pin names not known; wires that end beside it: PC[31:2], PC_4[31:2]

  assign PC_4[1:0] = PC[1:0];
endmodule

module Decoder (
  input  [31:0] Instr,
  output [15:0] Imm,
  output [4:0] rs,
  output [4:0] rt,
  output [4:0] rd,
  output [3:0] DummyALU,
  output [4:0] shamt,
  output ImmMux,
  output DummyWBMUX,
  output Write_Enable_Register,
  output DummyWED
);

  wire nand_1_out, nor_2_out, not_1_out, not_2_out, not_3_out;

  not not_1 (not_1_out, Instr[27]);
  not not_2 (not_2_out, Instr[30]);
  nor nor_1 (DummyWBMUX, Instr[28], Instr[26], Instr[27], Instr[29], Instr[30], Instr[31]);
  nor nor_2 (nor_2_out, not_1_out, Instr[28], Instr[29], Instr[30], Instr[31]);
  nand nand_1 (nand_1_out, Instr[29], not_2_out, Instr[31]);
  not not_3 (not_3_out, nor_2_out);
  nor nor_3 (ImmMux, DummyWBMUX, nor_2_out);
  and and_1 (Write_Enable_Register, not_3_out, nand_1_out);
  assign DummyALU = {{3{1'b0}}, DummyWBMUX};  // Bit_Extender bit_extender_1

  assign DummyWED = DummyWBMUX;
  assign Imm = Instr[15:0];
  assign rd = Instr[15:11];
  assign rs = Instr[25:21];
  assign rt = Instr[20:16];
  assign shamt = Instr[10:6];

  // Notes on the sheet:
  //   J Type
  //   R Type
  //   I Type
endmodule

module Isolator_2_3 (
  input  [4:0] rs_in,
  input  [4:0] rt_in,
  input  [31:0] PC_in,
  input  [15:0] Imm_in,
  input  [31:0] A_in,
  input  [31:0] B_in,
  input  [4:0] rd_in,
  input  [3:0] op_in,
  input  [4:0] sa_in,
  input  IE_in,
  input  WBMUX_in,
  input  WER_in,
  input  WED_in,
  input  clock,
  output [4:0] rs_out,
  output [4:0] rt_out,
  output [31:0] PC_out,
  output [15:0] Imm_out,
  output [31:0] A_out,
  output [31:0] B_out,
  output [4:0] rd_out,
  output [3:0] op_out,
  output [4:0] sa_out,
  output IE_out,
  output WBMUX_out,
  output WER_out,
  output WED_out
);

  Register #(.width(5)) rs (.D(rs_in), .Q(rs_out), .clk(clock));  // open: en, clr
  Register #(.width(5)) rt (.D(rt_in), .Q(rt_out), .clk(clock));  // open: en, clr
  Register #(.width(32)) PC (.D(PC_in), .Q(PC_out), .clk(clock));  // open: en, clr
  Register #(.width(16)) Imm (.D(Imm_in), .Q(Imm_out), .clk(clock));  // open: en, clr
  Register #(.width(32)) A (.D(A_in), .Q(A_out), .clk(clock));  // open: en, clr
  Register #(.width(32)) B (.D(B_in), .Q(B_out), .clk(clock));  // open: en, clr
  Register #(.width(5)) rd (.D(rd_in), .Q(rd_out), .clk(clock));  // open: en, clr
  Register #(.width(4)) aluop (.D(op_in), .Q(op_out), .clk(clock));  // open: en, clr
  Register #(.width(5)) sa (.D(sa_in), .Q(sa_out), .clk(clock));  // open: en, clr
  Register #(.width(1)) IE (.D(IE_in), .Q(IE_out), .clk(clock));  // open: en, clr
  Register #(.width(1)) WBMUX (.D(WBMUX_in), .Q(WBMUX_out), .clk(clock));  // open: en, clr
  Register #(.width(1)) WER (.D(WER_in), .Q(WER_out), .clk(clock));  // open: en, clr
  Register #(.width(1)) WED (.D(WED_in), .Q(WED_out), .clk(clock));  // open: en, clr
endmodule

module Isolate34 (
  input  [31:0] C_in,
  input  [31:0] PC_in,
  input  [4:0] rd_in,
  input  WBMUX_in,
  input  WER_in,
  input  WED_in,
  input  clock,
  output [31:0] C_out,
  output [31:0] PC_out,
  output [4:0] rd_out,
  output WBMUX_out,
  output WER_out,
  output WED_out
);

  Register #(.width(32)) PC (.D(C_in), .Q(C_out), .clk(clock));  // open: en, clr
  Register #(.width(32)) PC_2 (.D(PC_in), .Q(PC_out), .clk(clock));  // open: en, clr
  Register #(.width(5)) rd (.D(rd_in), .Q(rd_out), .clk(clock));  // open: en, clr
  Register #(.width(1)) WBMUX (.D(WBMUX_in), .Q(WBMUX_out), .clk(clock));  // open: en, clr
  Register #(.width(1)) WER (.D(WER_in), .Q(WER_out), .clk(clock));  // open: en, clr
  Register #(.width(1)) WED (.D(WED_in), .Q(WED_out), .clk(clock));  // open: en, clr
endmodule

module Isolate_45 (
  input  [31:0] C_in,
  input  [31:0] PC_in,
  input  [4:0] rd_in,
  input  WER_in,
  input  clock,
  output [31:0] C_out,
  output [31:0] PC_out,
  output [4:0] rd_out,
  output WER_out
);

  Register #(.width(32)) PC (.D(C_in), .Q(C_out), .clk(clock));  // open: en, clr
  Register #(.width(32)) PC_2 (.D(PC_in), .Q(PC_out), .clk(clock));  // open: en, clr
  Register #(.width(5)) rd (.D(rd_in), .Q(rd_out), .clk(clock));  // open: en, clr
  Register #(.width(1)) WER (.D(WER_in), .Q(WER_out), .clk(clock));  // open: en, clr
endmodule

module Forward (
  input  [31:0] Out2,
  input  [4:0] rd2,
  input  [4:0] rd1,
  input  [31:0] Out1,
  input  [4:0] rs,
  input  [31:0] Out0,
  output [31:0] Forwarded
);

  wire nor_1_out, nor_2_out;
  wire [4:0] xor_1_out, xor_2_out;
  wire [31:0] multiplexer_1_out;

  assign xor_1_out = rd1 ^ rs;  // XOR_Gate xor_1, 5 bits wide
  assign xor_2_out = rs ^ rd2;  // XOR_Gate xor_2, 5 bits wide
  nor nor_1 (nor_1_out, xor_1_out[0], xor_1_out[1], xor_1_out[2], xor_1_out[3], xor_1_out[4]);
  nor nor_2 (nor_2_out, xor_2_out[0], xor_2_out[1], xor_2_out[2], xor_2_out[3], xor_2_out[4]);
  Multiplexer #(.width(32), .enable("false")) multiplexer_1 (
    .in0(Out0), .in1(Out2), .out(multiplexer_1_out), .sel(nor_2_out));
  Multiplexer #(.width(32), .enable("false")) multiplexer_2 (
    .in0(multiplexer_1_out), .in1(Out1), .out(Forwarded), .sel(nor_1_out));
endmodule

module Isolate12 (
  input  [31:0] PC_in,
  input  [31:0] Instr_in,
  input  clock,
  output [31:0] PC_out,
  output [31:0] Instr_out
);

  Register #(.width(32)) PC (.D(PC_in), .Q(PC_out), .clk(clock));  // open: en, clr
  Register #(.width(32)) Instr (.D(Instr_in), .Q(Instr_out), .clk(clock));  // open: en, clr
endmodule
